// Logisim project Traffic.circ as structural Verilog: 1 circuit, main circuit main
module main (
  input  in_1,
  input  Reset
);

  wire and_4_out, and_5_out, and_6_out, and_7_out, d_ff_1_q, d_ff_2_q, not_1_out, not_2_out, or_1_out;

  D_Flip_Flop d_ff_1 (.clk(in_1), .D(in_1), .Q(d_ff_1_q), .en(in_1));  // open: Qn, preset, reset
  D_Flip_Flop d_ff_2 (.clk(d_ff_1_q), .D(in_1), .Q(d_ff_2_q), .Qn(in_1), .en(in_1));  // open: preset, reset
  not not_1 (not_1_out, in_1);
  not not_2 (not_2_out, d_ff_2_q);
  and and_1 (in_1, not_1_out, d_ff_2_q);
  and and_2 (in_1, in_1, in_1, d_ff_2_q);
  and and_3 (in_1, not_2_out, in_1);
  and and_4 (and_4_out, in_1, in_1);
  and and_5 (and_5_out, in_1, in_1);
  and and_6 (and_6_out, in_1, in_1);
  and and_7 (and_7_out, in_1, in_1);
  LED led_1 (.in(and_4_out));
  LED led_2 (.in(and_5_out));
  LED led_3 (.in(and_6_out));
  or or_1 (or_1_out, and_6_out, and_7_out);
  LED led_4 (.in(or_1_out));

  assign Reset = in_1;
endmodule
